# Fritzing sketch Svfs+RGB (saved by Fritzing 0.9.3b)

parts:
  KF-1 = KF-301 Relay [package=THT]
  U2 = ESP8266 NodeMCU LoLin module
  KF-2 = KF-301 Relay [package=THT]
  DHT1 = Humidity and Temperature Sensor DHT11
  Part1 = FC-28 Soil Hygrometer Module
  U3 = SWITCH-SPST-2 [package=r_sw_th]
  Battery_Output = Dagu DGServo 9g header (male) [package=THT]
  WATER_PUMP1 = water pump/motor
  F1 = Fan - Ventilador [package=THT]
  F2 = Fan - Ventilador [package=THT]
  Solar_Panel = SOLAR-IXYS [package=solarbit-12x1]
  Battery_Connector = Lilypad Battery Connect
  RGB_Strip_LED1 = RGB Strip LED
  Q1 = MOSFET-NCHANNEL [package=to220v]
  Q2 = MOSFET-NCHANNEL [package=to220v]
  Q3 = MOSFET-NCHANNEL [package=to220v]

nets:
  N1: KF-1.signal, U2.D3
  VCC: KF-1.power, U2.3V3, KF-2.power, DHT1.Vcc, Part1.VCC
  GND: KF-1.ground, U2.GND, DHT1.GND_1, Part1.GND, Battery_Output.gnd, WATER_PUMP1.pin_1, F1.GND
  N2: KF-1.C, U3.O, Battery_Output.pulse, RGB_Strip_LED1.Common_Connect
  N3: KF-1.NO, WATER_PUMP1.pin_2
  N4: U2.D0, Part1.DO
  N5: U2.D1, DHT1.Data-signal
  N6: U2.D2, KF-2.signal
  N7: U2.D5, Q1.G
  N8: U2.D6, Q2.G
  N9: U2.D7, Q3.G
  N10: U2.Vin, U3.P
  N11: U2.A0, Part1.AO
  5V: KF-2.NO, F1.5V, F2.5V
  N12: Solar_Panel.A, Battery_Connector.+
  N13: Solar_Panel.C, Battery_Connector.-
  N14: RGB_Strip_LED1.Green_Connect, Q2.D
  N15: RGB_Strip_LED1.Red_Connect, Q1.D
  N16: Q1.S, Q2.S, Q3.S

custom parts:
  KF-301 Relay: KF-301
  ESP8266 NodeMCU LoLin module: ESP8266 based NodeMCU
  Humidity and Temperature Sensor DHT11: Digital relative humidity & temperature sensor DHT11
  FC-28 Soil Hygrometer Module: The FC-28 is a soil hygrometer module that uses the Texas Instruments LM393 comparator chip to provide an analog measurement of soil humidity. The digital output is high when soil moisture is over a certain threshold, as determined by adjusting the potentiometer.
  water pump/motor: WATER PUMP BY ARDUBLOCKTR
  Fan - Ventilador: Ventilador de 2 pines, se encuentra comunmente en computadoras de escritorio
  RGB Strip LED: A tri-color Strip LED with red, green and blue. Based on LED SMD 5050 RGB Pin order: common cathode - green - red - blue
