# Fritzing sketch Svfs-Dual (saved by Fritzing 0.9.3b)

parts:
  KF-1 = KF-301 Relay [package=THT]
  U2 = ESP8266 NodeMCU LoLin module
  KF-2 = KF-301 Relay [package=THT]
  DHT1 = Humidity and Temperature Sensor DHT11
  Part1 = FC-28 Soil Hygrometer Module
  U3 = SWITCH-SPST-2 [package=r_sw_th]
  Battery_Output = Dagu DGServo 9g header (male) [package=THT]
  WATER_PUMP1 = water pump/motor
  F1 = Fan - Ventilador [package=THT]
  F2 = Fan - Ventilador [package=THT]
  Solar_Panel = SOLAR-IXYS [package=solarbit-12x1]
  Battery_Connector = Lilypad Battery Connect
  RGB_Strip_LED2 = RGB Strip LED
  Q4 = MOSFET-NCHANNEL [package=to220v]
  Q5 = MOSFET-NCHANNEL [package=to220v]
  Q6 = MOSFET-NCHANNEL [package=to220v]
  F3 = Fan - Ventilador [package=THT]
  F4 = Fan - Ventilador [package=THT]
  WATER_PUMP2 = water pump/motor
  Part2 = FC-28 Soil Hygrometer Module
  U4 = SWITCH-SPST-2 [package=r_sw_th]
  Battery_Output1 = Dagu DGServo 9g header (male) [package=THT]
  DHT2 = Humidity and Temperature Sensor DHT11
  KF-3 = KF-301 Relay [package=THT]
  U5 = ESP8266 NodeMCU LoLin module
  KF-4 = KF-301 Relay [package=THT]

nets:
  N1: KF-1.signal, U2.D3
  VCC: KF-1.power, U2.3V3, KF-2.power, DHT1.Vcc, Part1.VCC
  GND: KF-1.ground, U2.GND, DHT1.GND_1, Part1.GND, Battery_Output.gnd, WATER_PUMP1.pin_1, F1.GND
  N2: KF-1.C, U3.O, Battery_Output.pulse, RGB_Strip_LED2.Common_Connect, U4.O, Battery_Output1.pulse, KF-4.C
  N3: KF-1.NO, WATER_PUMP1.pin_2
  N4: U2.D0, Part1.DO
  N5: U2.D1, DHT1.Data-signal
  N6: U2.D2, KF-2.signal
  N7: U2.Vin, U3.P
  N8: U2.A0, Part1.AO
  5V: KF-2.NO, F1.5V, F2.5V
  N9: Solar_Panel.A, Battery_Connector.+
  N10: Solar_Panel.C, Battery_Connector.-
  N11: RGB_Strip_LED2.Green_Connect, Q5.D
  N12: RGB_Strip_LED2.Red_Connect, Q6.D
  N13: Q4.G, U5.D7
  N14: Q4.S, Q5.S, Q6.S
  N15: Q5.G, U5.D6
  N16: Q6.G, U5.D5
  5V_2: F3.5V, F4.5V, KF-3.NO
  GND_2: F4.GND, Part2.GND, Battery_Output1.gnd, DHT2.GND_1, U5.GND, KF-4.ground
  N17: WATER_PUMP2.pin_2, KF-4.NO
  VCC_2: Part2.VCC, DHT2.Vcc, KF-3.power, U5.3V3, KF-4.power
  N18: Part2.DO, U5.D0
  N19: Part2.AO, U5.A0
  N20: U4.P, U5.Vin
  N21: DHT2.Data-signal, U5.D1
  N22: KF-3.signal, U5.D2
  N23: U5.D3, KF-4.signal

custom parts:
  KF-301 Relay: KF-301
  ESP8266 NodeMCU LoLin module: ESP8266 based NodeMCU
  Humidity and Temperature Sensor DHT11: Digital relative humidity & temperature sensor DHT11
  FC-28 Soil Hygrometer Module: The FC-28 is a soil hygrometer module that uses the Texas Instruments LM393 comparator chip to provide an analog measurement of soil humidity. The digital output is high when soil moisture is over a certain threshold, as determined by adjusting the potentiometer.
  water pump/motor: WATER PUMP BY ARDUBLOCKTR
  Fan - Ventilador: Ventilador de 2 pines, se encuentra comunmente en computadoras de escritorio
  RGB Strip LED: A tri-color Strip LED with red, green and blue. Based on LED SMD 5050 RGB Pin order: common cathode - green - red - blue
